// Logisim project KMAP.circ as structural Verilog
module _1 (
  input  A,
  input  B,
  input  C,
  input  D,
  output F
);

  wire and_1_out, and_2_out, and_3_out, not_1_out, not_2_out;

  and and_1 (and_1_out, B, C);
  not not_1 (not_1_out, A);
  and and_2 (and_2_out, not_1_out, B);
  and and_3 (and_3_out, A, not_2_out);
  not not_2 (not_2_out, C);
  or or_1 (F, and_1_out, and_2_out, and_3_out);
endmodule

module _2 (
  input  A,
  input  B,
  input  C,
  input  D,
  output F
);

  wire nand_1_out, nand_2_out, nand_3_out, nand_4_out, nand_5_out, nand_6_out, nand_7_out, nand_8_out,
       nand_9_out, nand_10_out, nand_11_out, nand_12_out, nand_13_out;

  nand nand_1 (nand_1_out, A, A);
  nand nand_2 (nand_2_out, B, B);
  nand nand_3 (nand_3_out, A, A);
  nand nand_4 (nand_4_out, C, C);
  nand nand_5 (nand_5_out, D, D);
  nand nand_6 (nand_6_out, B, B);
  nand nand_7 (nand_7_out, D, D);
  nand nand_8 (nand_8_out, C, C);
  nand nand_9 (nand_9_out, D, D);
  nand nand_10 (nand_10_out, nand_1_out, nand_2_out, C, D);
  nand nand_11 (nand_11_out, nand_3_out, B, nand_4_out, nand_5_out);
  nand nand_12 (nand_12_out, A, nand_6_out, C, nand_7_out);
  nand nand_13 (nand_13_out, A, B, nand_8_out, nand_9_out);
  nand nand_14 (F, nand_10_out, nand_11_out, nand_12_out, nand_13_out);
endmodule

module _3 (
  input  A,
  input  B,
  input  C,
  input  D,
  output F
);

  wire nand_1_out, nand_2_out, nand_3_out, nand_4_out, nand_5_out, nand_6_out, nand_7_out, nand_8_out,
       nand_9_out, nand_10_out, nand_11_out, nand_12_out, nand_13_out, nand_14_out;

  nand nand_1 (nand_1_out, A, A);
  nand nand_2 (nand_2_out, B, B);
  nand nand_3 (nand_3_out, C, C);
  nand nand_4 (nand_4_out, D, D);
  nand nand_5 (nand_5_out, A, A);
  nand nand_6 (nand_6_out, D, D);
  nand nand_7 (nand_7_out, A, A);
  nand nand_8 (nand_8_out, B, B);
  nand nand_9 (nand_9_out, C, C);
  nand nand_10 (nand_10_out, D, D);
  nand nand_11 (nand_11_out, nand_1_out, nand_2_out, nand_3_out, nand_4_out);
  nand nand_12 (nand_12_out, nand_5_out, B, C, nand_6_out);
  nand nand_13 (nand_13_out, nand_7_out, B, C, D);
  nand nand_14 (nand_14_out, A, nand_8_out, nand_9_out, nand_10_out);
  nand nand_15 (F, nand_11_out, nand_12_out, nand_13_out, nand_14_out);
endmodule
