// Logisim project kmaplogisim2.circ as structural Verilog
module kmaplogisim (
  input  w,
  input  x,
  input  y,
  input  z,
  output f
);

  wire and_1_out, not_1_out;

  not not_1 (not_1_out, w);
  and and_1 (and_1_out, not_1_out, x);
  or or_1 (f, z, and_1_out);
endmodule

module kmaplogisim2 (
  input  A,
  input  B,
  input  C,
  input  D,
  output F
);

  wire and_1_out, and_2_out, and_3_out, and_4_out, and_5_out, not_1_out, not_2_out, not_3_out, or_1_out;

  not not_1 (not_1_out, A);
  and and_1 (and_1_out, A, B);
  not not_2 (not_2_out, C);
  and and_2 (and_2_out, not_1_out, C);
  or or_1 (or_1_out, and_2_out, and_3_out);
  and and_3 (and_3_out, and_1_out, not_2_out);
  and and_4 (and_4_out, A, B);
  and and_5 (and_5_out, and_4_out, not_3_out);
  not not_3 (not_3_out, D);
  or or_2 (F, or_1_out, and_5_out);
endmodule
